# Fritzing sketch MiniMonitor (saved by Fritzing 0.9.5d)
breadboards: 1

parts:
  Part1 = Arduino Uno (Rev3)
  IC2 = AD8232 HeartRate Monitor [part_number=SEN-12650 chip_label=IC package="DIP (Dual Inline) [THT]"]
  M2 = MakerFocus MAX30102
  J1 = Piezo Speaker
  R1 = Resistor [tolerance=±5% resistance=100 package=THT]

nets:
  N1: Part1.A0, IC2.OUTPUT
  N2: Part1.D9_PWM, R1.Pin_0
  N3: Part1.D10_PWM/SS, IC2.LO+
  N4: Part1.D11_PWM/MOSI, IC2.LO-
  GND: Part1.GND, IC2.GND, M2.GND, J1.pin1
  N5: Part1.A4/SDA, M2.SDA
  N6: Part1.A5/SCL, M2.SCL
  3V3: Part1.3V3, IC2.3.3v
  5V: Part1.5V, M2.VIN
  N7: J1.pin2, R1.Pin_1

custom parts:
  AD8232 HeartRate Monitor: A DIP stand-in part for whatever IC you want. With 10 pins on a 600mil dual inline package (DIP) footprint.
  MakerFocus MAX30102: Oximeter module using the MAX30102 chip. As usual, if you want the mounting holes in pcb, you need to drag a hole over the pad in silkscreen to actually drill the hole (by default they are not drilled)
